# Fritzing sketch Schaltplan (saved by Fritzing 0.9.3b)
breadboards: 1

parts:
  Raspberry_Pi_Zero1 = Raspberry Pi Zero
  U1 = TCM8240MD [package=tcm8240md]  # not connected
  PIR1 = PIR sensor

nets:
  3V3: Raspberry_Pi_Zero1.3v3, PIR1.VDD
  GND: Raspberry_Pi_Zero1.GND, PIR1.GND
  N1: Raspberry_Pi_Zero1.GPIO17, PIR1.SIG
